// Logisim project project.circ as structural Verilog: 3 circuits, main circuit STATE_CONTROLLER
module STATE_CONTROLLER (
  input  Q2,
  input  Q1,
  input  Q0,
  output D2,
  output D1,
  output D0
);

  wire not_1_out, not_2_out, not_3_out, not_4_out, xor_1_out;

  not not_1 (not_1_out, Q2);
  not not_2 (not_2_out, Q0);
  and and_1 (D0, not_1_out, not_2_out);
  not not_3 (not_3_out, Q2);
  not not_4 (not_4_out, Q2);
  xor xor_1 (xor_1_out, Q1, Q0);
  and and_2 (D2, not_3_out, Q1, Q0);
  and and_3 (D1, not_4_out, xor_1_out);
endmodule

module main_circuit (
);

  wire clock_1_out, FF0_q, FF1_q, FF2_q, state_controller_1_d0, state_controller_1_d1, state_controller_1_d2,
       traffic_light_controller_1_gp, traffic_light_controller_1_gv, traffic_light_controller_1_rp,
       traffic_light_controller_1_rv, traffic_light_controller_1_yv;

  Clock clock_1 (.out(clock_1_out));
  D_Flip_Flop FF2 (.D(state_controller_1_d2), .clk(clock_1_out), .Q(FF2_q));  // open: Qn, preset, reset
  D_Flip_Flop FF1 (.D(state_controller_1_d1), .clk(clock_1_out), .Q(FF1_q));  // open: Qn, preset, reset
  STATE_CONTROLLER state_controller_1 (
    .Q2(FF2_q), .Q1(FF1_q), .Q0(FF0_q), .D2(state_controller_1_d2), .D1(state_controller_1_d1),
    .D0(state_controller_1_d0));
  D_Flip_Flop FF0 (.D(state_controller_1_d0), .clk(clock_1_out), .Q(FF0_q));  // open: Qn, preset, reset
  TRAFFIC_LIGHT_CONTROLLER traffic_light_controller_1 (
    .Q2(FF2_q), .Q1(FF1_q), .Q0(FF0_q), .Gv(traffic_light_controller_1_gv),
    .Yv(traffic_light_controller_1_yv), .Rv(traffic_light_controller_1_rv),
    .Gp(traffic_light_controller_1_gp), .Rp(traffic_light_controller_1_rp));
  LED Gv (.in(traffic_light_controller_1_gv));
  LED Yv (.in(traffic_light_controller_1_yv));
  LED Rv (.in(traffic_light_controller_1_rv));
  LED Gp (.in(traffic_light_controller_1_gp));
  LED Rp (.in(traffic_light_controller_1_rp));
  Clock CLK ();  // open: out
endmodule

module TRAFFIC_LIGHT_CONTROLLER (
  input  Q2,
  input  Q1,
  input  Q0,
  output Gv,
  output Yv,
  output Rv,
  output Gp,
  output Rp
);

  wire and_4_out, not_1_out, not_2_out, not_3_out, not_4_out, not_5_out, not_6_out, not_7_out, not_8_out,
       not_9_out, or_1_out;

  not not_1 (not_1_out, Q2);
  not not_2 (not_2_out, Q1);
  not not_3 (not_3_out, Q0);
  or or_1 (or_1_out, not_2_out, not_3_out);
  not not_4 (not_4_out, Q2);
  and and_1 (Gv, not_1_out, or_1_out);
  not not_5 (not_5_out, Q1);
  not not_6 (not_6_out, Q0);
  not not_7 (not_7_out, Q2);
  not not_8 (not_8_out, Q1);
  not not_9 (not_9_out, Q0);
  and and_2 (Yv, not_4_out, Q1, Q0);
  and and_3 (Rv, Q2, not_5_out, not_6_out);
  and and_4 (and_4_out, not_7_out, Q1, Q0);
  and and_5 (Gp, Q2, not_8_out, not_9_out);
  or or_2 (Rp, Gv, and_4_out);
endmodule
